// Logisim project AspiradoraTrabajando.circ as structural Verilog: 1 circuit, main circuit main
module main (
  input  on_off,
  input  suciedad,
  input  obstaculo,
  input  CLK,
  output Q0,
  output Q1
);

  wire and_1_out, and_2_out, and_3_out, and_4_out, and_5_out, and_6_out, and_7_out, and_8_out, and_9_out,
       and_10_out, not_1_out, not_2_out, not_3_out, not_4_out, not_5_out, not_6_out, or_1_out, or_2_out,
       or_3_out, or_4_out, S0_qn, S1_qn;

  and and_1 (and_1_out, Q0, S1_qn, obstaculo);
  not not_1 (not_1_out, obstaculo);
  and and_2 (and_2_out, Q1, suciedad);
  and and_3 (and_3_out, Q0, Q1, not_1_out);
  or or_1 (or_1_out, and_1_out, and_3_out);
  not not_2 (not_2_out, obstaculo);
  and and_4 (and_4_out, Q0, S1_qn, not_2_out);
  and and_5 (and_5_out, S0_qn, Q1, obstaculo);
  S_R_Flip_Flop S0 (.S(or_2_out), .R(or_1_out), .clk(CLK), .Q(Q0), .Qn(S0_qn));  // open: reset, preset
  or or_2 (or_2_out, and_2_out, and_4_out, and_5_out);
  not not_3 (not_3_out, on_off);
  not not_4 (not_4_out, suciedad);
  not not_5 (not_5_out, obstaculo);
  and and_6 (and_6_out, not_3_out, S0_qn, not_4_out);
  and and_7 (and_7_out, Q0, Q1, not_5_out, suciedad);
  or or_3 (or_3_out, and_6_out, and_7_out);
  not not_6 (not_6_out, suciedad);
  and and_8 (and_8_out, S0_qn, S1_qn, on_off);
  and and_9 (and_9_out, S1_qn, Q0, not_6_out);
  or or_4 (or_4_out, and_8_out, and_9_out, and_10_out);
  and and_10 (and_10_out, S0_qn, S1_qn, suciedad);
  S_R_Flip_Flop S1 (.S(or_4_out), .R(or_3_out), .clk(CLK), .Q(Q1), .Qn(S1_qn));  // open: reset, preset

  // Other names for the same wires on the sheet: out_Q0 = Q0; out_Q1 = Q1
endmodule
